# Fritzing sketch FilterEye_v3 (saved by Fritzing 0.9.9b)
circuit board: 8.3449cm x 6.34601cm
breadboards: 1

parts:
  pressure_local = Adafruit DPS310 Precision Barometric Pressure and Altitude Sensor [part_number="Adafruit #4494"]
  light_sensor = Flora TCS34725 Color Sensor
  pressure_remote = Adafruit DPS310 Precision Barometric Pressure and Altitude Sensor [part_number="Adafruit #4494"]
  button = Pushbutton [package="[THT]"]
  cr2032_battery = Battery Holders [package=battcom_20mm_pth]
  aux_male = female pin header, 4 pins [form="♀ (female)"]
  aux_female = TRRS 3.5mm Jack Breakout
  nrf_right = female pin header, 12 pins [form="♀ (female)"]
  vcc_select = female pin header, 3 pins [form="♀ (female)"]
  R_pull_down = Resistor [tolerance=±5% power=0.25 resistance=100k package=THT]
  nrf_up = female pin header, 12 pins [form="♀ (female)"]
  light_local = female pin header, 4 pins [form="♀ (female)"]
  light_remote = female pin header, 4 pins [form="♀ (female)"]
  nrf_left = female pin header, 2 pins [form="♀ (female)"]
  buzzer = female pin header, 4 pins [form="♀ (female)"]
  progamming = Header 5x2 [package=2x5-ra]

nets:
  N1: pressure_local.VCC, aux_male.pin1, nrf_up.pin8, light_local.pin4
  N2: pressure_local.SDI/SDA, aux_male.pin3, nrf_up.pin7, light_local.pin3
  N3: pressure_local.SCK/SCL, aux_male.pin2, nrf_up.pin6, light_local.pin2
  N4: pressure_local.GND, cr2032_battery.-, aux_male.pin4, nrf_right.pin3, R_pull_down.Pin_1, light_local.pin1, buzzer.pin4
  N5: light_sensor.3.3V, light_remote.pin4
  N6: light_sensor.GND, light_remote.pin1
  N7: light_sensor.SDA_3V, light_remote.pin3
  N8: light_sensor.SCL_3V, light_remote.pin2
  N9: pressure_remote.VCC, aux_female.TIP
  N10: pressure_remote.GND, aux_female.SLEEVE
  N11: pressure_remote.SCK/SCL, aux_female.RING1
  N12: pressure_remote.SDI/SDA, aux_female.RING2
  N13: button.Pin_1, button.Pin_2, R_pull_down.Pin_0, nrf_up.pin5
  N14: button.Pin_3, button.Pin_4, nrf_right.pin2, vcc_select.pin2
  N15: cr2032_battery.+, vcc_select.pin3
  N16: nrf_right.pin7, progamming.4
  N17: nrf_right.pin8, progamming.2
  N18: vcc_select.pin1, progamming.3
  N19: nrf_up.pin4, buzzer.pin1
  N20: nrf_left.pin1, progamming.9
  N21: nrf_left.pin2, progamming.5

notes:
  0x77
  0x76
  nrf unit
  P0.16
  P0.17
  P0.18
  P0.19
  P0.20
  P0.21
  SW
  SCLK
  P0.22
  P0.24
  P0.23
  JP3
  JP2
  P0.04
  P0.05
  SCL/P0.10
  P0.07
  P0.06
  P0.08
  SDA/P0.09
  P0.11
  P0.12
  P0.13
  P0.14
  P0.15
  NC
  P0.27
  P0.30/Rx
  P0.02
  P0.26
  GND
  P0.03
  P0.29/Tx
  P0.28
  VCC
  P0.31
  P0.25
  JP1
  5V
  3V3
  Rx
  Tx
  nRST
  TDO
  TDI
  BATT VCC
  NRF VCC
  USB VCC
  GPIO VCC
  ring1 (SDI)
  ring2 (SCK)
  sleeve (GND)
  tip (VIN)
  cr2032
  +
  -
  FilterEye V1
  February 2023
  batt
  USB
  nrf
  s/gnd
  r2/sdi
  sda
  r1/sck
  scl
  t/vin
  vcc
  gnd
  r2/sdi/sda
  r1/sck/scl
  t/vin/vcc

custom parts:
  Adafruit DPS310 Precision Barometric Pressure and Altitude Sensor: How high are you right now? If you had a precision altitude sensor, you would know for sure! The DPS310 sensor from Infineon a high precision barometric sensor, perfect for measuring altitude changes with a up to ±0.002 hPa (or ±0.02 m) precision high precision mode and ± 1 hPa absolute accuracy. That means you can know your absolute altitude with 1 meter accuracy when you set the sea-level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
  Flora TCS34725 Color Sensor: Your electronics can now see in dazzling color with this lovely color light sensor. We found the best color sensor on the market, the TCS34725, which has RGB and Clear light sensing elements. An IR blocking filter, integrated on-chip and localized to the color sensing photodiodes, minimizes the IR spectral component of the incoming light and allows color measurements to be made accurately. The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
